# Fritzing sketch blueprint-max (saved by Fritzing 0.9.9b)
stripboards: 1

parts:
  Mod1 = Raspberry Pi 4B
  M1 = DC Motor
  M2 = DC Motor
  M3 = DC Motor
  M4 = DC Motor
  M5 = DC Motor  # not connected
  M6 = DC Motor
  M7 = DC Motor  # not connected
  M8 = DC Motor  # not connected
  DRV_1 = DRV 8825 Stepper Motor Carrier, High Current [part_number="DRV 8825"]
  M9 = Stepper Motor - Bipolar
  J1 = XL4015 DC-DC CC CV module (blue)
  Power_plug2 = Power plug [part_number=9V]
  J2 = XL4015 DC-DC CC CV module (blue)
  Waveshare_MCP23017_Breakout1 = Waveshare MCP23017 Breakout
  DRV_2 = DRV 8825 Stepper Motor Carrier, High Current [part_number="DRV 8825"]
  M10 = Stepper Motor - Bipolar
  DRV_3 = DRV 8825 Stepper Motor Carrier, High Current [part_number="DRV 8825"]
  M11 = Stepper Motor - Bipolar
  DRV_4 = DRV 8825 Stepper Motor Carrier, High Current [part_number="DRV 8825"]
  M12 = Stepper Motor - Bipolar
  D1 = Rectifier Diode [part_number=1N4001 package="300 mil [THT]"]
  J3 = Camdenboss CTB0158-2 [part_number=CTB0158-2 package=THT]
  J4 = Camdenboss CTB0158-2 [part_number=CTB0158-2 package=THT]
  J5 = Camdenboss CTB0158-2 [part_number=CTB0158-2 package=THT]
  J6 = Camdenboss CTB0158-2 [part_number=CTB0158-2 package=THT]
  J7 = Camdenboss CTB0158-2 [part_number=CTB0158-2 package=THT]
  J8 = Camdenboss CTB0158-2 [part_number=CTB0158-2 package=THT]
  J9 = Camdenboss CTB0158-12 [part_number=CTB0158-12 package=THT]
  J10 = Camdenboss CTB0158-12 [part_number=CTB0158-12 package=THT]
  U1 = 2-Channel 5v Relay Shield [package=relay-2ch5v10a]
  8_Channel_Relay1 = 8 Channel Power Relay
  J11 = Camdenboss CTB0158-12 [part_number=CTB0158-12 package=THT]  # not connected
  J12 = Camdenboss CTB0158-12 [part_number=CTB0158-12 package=THT]  # not connected
  J13 = Camdenboss CTB0158-11 [part_number=CTB0158-11 package=THT]
  J14 = Camdenboss CTB0158-2 [part_number=CTB0158-2 package=THT]
  J15 = Camdenboss CTB0158-2 [part_number=CTB0158-2 package=THT]
  J16 = Camdenboss CTB0158-2 [part_number=CTB0158-2 package=THT]

nets:
  N1: Mod1.GPIO2, Waveshare_MCP23017_Breakout1.SDA
  N2: Mod1.GPIO3, Waveshare_MCP23017_Breakout1.SCL
  N3: Mod1.GND, J10.terminal_1
  N4: Mod1.GPIO4, DRV_1.ENABLE
  N5: Mod1.GPIO14, DRV_1.STEP
  N6: Mod1.GPIO15, DRV_2.STEP
  N7: Mod1.GPIO17, DRV_2.ENABLE
  N8: Mod1.GPIO18, DRV_3.STEP
  N9: Mod1.GPIO27, DRV_3.ENABLE
  N10: Mod1.GPIO22, DRV_4.ENABLE
  N11: Mod1.GPIO23, DRV_4.STEP
  N12: Mod1.GPIO24, J13.terminal_11
  N13: Mod1.GPIO25, 8_Channel_Relay1.IN1
  N14: Mod1.GPIO8, 8_Channel_Relay1.IN2
  N15: Mod1.GPIO7, 8_Channel_Relay1.IN3
  N16: Mod1.ID_SC, 8_Channel_Relay1.IN4
  N17: Mod1.GPIO12, 8_Channel_Relay1.IN5
  N18: Mod1.GPIO16, 8_Channel_Relay1.IN6
  N19: Mod1.GPIO20, 8_Channel_Relay1.IN7
  N20: Mod1.GPIO21, 8_Channel_Relay1.IN8
  N21: M1.pin_1, M6.pin_1
  N22: M2.pin_1, 8_Channel_Relay1.NO#26
  N23: M2.pin_2, M4.pin_2, U1.K1-In
  N24: M3.pin_1, 8_Channel_Relay1.NO#32
  N25: DRV_1.DIRECTION, J13.terminal_6
  N26: DRV_1.VOLTAGE_ST/_MT, J1.pin_1, Power_plug2.VCC, J2.pin_1, J6.pin2, J7.pin2, J8.pin2
  N27: DRV_1.GROUND_ST/_MT, J1.pin_2, Power_plug2.GND, J2.pin_2, J3.pin2, J4.pin2, J5.pin2
  N28: DRV_1.OUT_2B, M9.A
  N29: DRV_1.OUT_2A, M9.C
  N30: DRV_1.OUT_1A, M9.B
  N31: DRV_1.OUT_1B, M9.D
  N32: DRV_1.GROUND_LOG, J10.terminal_10, J14.pin2, J15.pin2, J16.pin2
  N33: J1.pin_3, D1.cathode, U1.K1-On, U1.K2-Off
  N34: J1.pin_4, D1.anode, U1.K1-Off, U1.K2-On
  N35: J2.pin_3, J9.terminal_1
  N36: J2.pin_4, J10.terminal_12
  N37: Waveshare_MCP23017_Breakout1.Vcc, J9.terminal_12
  N38: Waveshare_MCP23017_Breakout1.GND, J10.terminal_2
  N39: DRV_2.DIRECTION, J13.terminal_5
  N40: DRV_2.VOLTAGE_ST/_MT, J8.pin1
  N41: DRV_2.GROUND_ST/_MT, J3.pin1
  N42: DRV_2.OUT_2B, M10.A
  N43: DRV_2.OUT_2A, M10.C
  N44: DRV_2.OUT_1A, M10.B
  N45: DRV_2.OUT_1B, M10.D
  N46: DRV_2.GROUND_LOG, J14.pin1
  N47: DRV_3.DIRECTION, J13.terminal_4
  N48: DRV_3.VOLTAGE_ST/_MT, J6.pin1
  N49: DRV_3.GROUND_ST/_MT, J4.pin1
  N50: DRV_3.OUT_2B, M11.A
  N51: DRV_3.OUT_2A, M11.C
  N52: DRV_3.OUT_1A, M11.B
  N53: DRV_3.OUT_1B, M11.D
  N54: DRV_3.GROUND_LOG, J15.pin1
  N55: DRV_4.DIRECTION, J13.terminal_3
  N56: DRV_4.VOLTAGE_ST/_MT, J7.pin1
  N57: DRV_4.GROUND_ST/_MT, J5.pin1
  N58: DRV_4.OUT_2B, M12.A
  N59: DRV_4.OUT_2A, M12.C
  N60: DRV_4.OUT_1A, M12.B
  N61: DRV_4.OUT_1B, M12.D
  N62: DRV_4.GROUND_LOG, J16.pin1
  N63: J9.terminal_2, U1.VCC
  N64: J9.terminal_11, 8_Channel_Relay1.VCC
  N65: J10.terminal_3, 8_Channel_Relay1.GND
  N66: J10.terminal_11, U1.GND
  N67: U1.IN1, J13.terminal_2
  N68: U1.IN2, J13.terminal_1
  N69: U1.K2-In, 8_Channel_Relay1.COM

notes:
  RaspberryPi 4B 2GB Ram
  peristaltic pump
  8-channel relais board
  WiringPi 9
  WiringPi 8
  WiringPi 7
  WiringPi 12
  WiringPi 13
  WiringPi 14
  WiringPi 21
  WiringPi 22
  Voltage director relays
  Main Power source (24V)
  Power converter (9V)
  Power converter (5V)
  MCP23017 I2C Pinexpander
  SDA
  SCL
  Rectifier diode
  Logic power (5V)
  Direction Pins
  Not used here. Just an example.

custom parts:
  XL4015 DC-DC CC CV module (blue): XL4015 DC-DC CC/CV module blue
  Waveshare MCP23017 Breakout: MCP23017 Breakout board - I2C 16bit I/O Expander
  2-Channel 5v Relay Shield: 2 Channel 5v Relay Shield w. 2x SPD-06VDC-SD-C
  8 Channel Power Relay: An 8 channel power relay. The module operates at 5V.
