# Fritzing sketch blueprint-vd (saved by Fritzing 0.9.9b)
stripboards: 1

parts:
  Mod1 = Raspberry Pi 4B
  8_Channel_Relay1 = 8 Channel Power Relay
  M1 = DC Motor
  M2 = DC Motor
  M3 = DC Motor
  M4 = DC Motor
  M5 = DC Motor  # not connected
  M6 = DC Motor
  M7 = DC Motor  # not connected
  M8 = DC Motor  # not connected
  Mod2 = KY-019 5V Relay Module [package="Breakout board"]
  Mod3 = KY-019 5V Relay Module [package="Breakout board"]
  Power_plug1 = Power plug [part_number=9V]
  D1 = Rectifier Diode [part_number=1N4001 package="300 mil [THT]"]

nets:
  5V: Mod1.5V, 8_Channel_Relay1.VCC, Mod2.+, Mod3.+
  N1: Mod1.GPIO2, 8_Channel_Relay1.IN1
  N2: Mod1.GPIO3, 8_Channel_Relay1.IN2
  GND: Mod1.GND, Mod1.GPIO17, 8_Channel_Relay1.GND, Mod2.-, Mod3.-
  N3: Mod1.GPIO4, 8_Channel_Relay1.IN3
  N4: Mod1.GPIO23, Mod2.S, Mod3.S
  N5: Mod1.GPIO10, 8_Channel_Relay1.IN4
  N6: Mod1.GPIO9, 8_Channel_Relay1.IN5
  N7: Mod1.GPIO11, 8_Channel_Relay1.IN6
  N8: Mod1.GPIO5, 8_Channel_Relay1.IN7
  N9: Mod1.GPIO6, 8_Channel_Relay1.IN8
  N10: 8_Channel_Relay1.COM, Mod3.Common
  N11: 8_Channel_Relay1.NO#26, M2.pin_1
  N12: 8_Channel_Relay1.NO#32, M3.pin_1
  N13: M1.pin_1, M6.pin_1
  N14: M2.pin_2, M4.pin_2, Mod2.Common
  N15: Mod2.NC, Mod3.NO, Power_plug1.GND, D1.anode
  N16: Mod2.NO, Mod3.NC, Power_plug1.VCC, D1.cathode

notes:
  RaspberryPi 4B 2GB Ram
  peristaltic pump
  8-channel relais board
  WiringPi 9
  WiringPi 8
  WiringPi 7
  WiringPi 12
  WiringPi 13
  WiringPi 14
  WiringPi 21
  WiringPi 22
  Voltage director relays
  Power source
  Rectifier Diode

custom parts:
  8 Channel Power Relay: An 8 channel power relay. The module operates at 5V.
  KY-019 5V Relay Module: KY-019 5V Relay module, used to control AC circuits. (Special thanks to vanepp for fixing the PCB holes and other errors)
